# Fritzing sketch Aufbau (saved by Fritzing 0.9.3b)
stripboards: 2

parts:
  Cortex = Raspberry Pi 3 [part_number=RPI-3-V1.2]
  Lenkung = Basic Servo
  Polulu_Motor_Controller = Dual VNH2SP30 Motor Driver [part_number=MD03A]
  Motor-Akku = 4 x AAA Battery Mount
  Motor = DC Motor
  U2 = Voltage Regulator - 5V [package="TO220 [THT]"]
  US-Front = 28015 Ultrasonic Digital Sensor [package=THT]
  US-Seite = 28015 Ultrasonic Digital Sensor [package=THT]
  RPi-Akku = 4 x AAA Battery Mount
  Driver = Arduino Uno (Rev3) - ICSP

nets:
  GND: Cortex.GND, Cortex.GIPO18, Lenkung.pulse, US-Front.GND, US-Seite.GND, RPi-Akku.-
  N1: Cortex.GIPO15, Driver.D1/TX
  N2: Cortex.GIPO14, Driver.D0/RX
  5V: Cortex.5V, US-Front.5V, US-Seite.5V, RPi-Akku.+, Driver.5V
  GND_2: Lenkung.gnd, Polulu_Motor_Controller.GND#151, Motor-Akku.-, U2.GND
  N3: Lenkung.vcc, U2.output_voltage
  N4: Polulu_Motor_Controller.PWM, Driver.D11_PWM/MOSI
  N5: Polulu_Motor_Controller.GND#138, Driver.GND
  N6: Polulu_Motor_Controller.OUT_1A, Motor.pin_1
  N7: Polulu_Motor_Controller.OUT_1B, Motor.pin_2
  N8: Polulu_Motor_Controller.VIN, Motor-Akku.+, U2.input_voltage
  N9: US-Front.SIG, Driver.D7
  N10: US-Seite.SIG, Driver.D8

custom parts:
  28015 Ultrasonic Digital Sensor: This is the 28015 ultrasonic digital sensor from parallax inf
