# Fritzing sketch Aufbau (saved by Fritzing 0.9.3b)
stripboards: 1

parts:
  Cortex = Raspberry Pi 3 [part_number=RPI-3-V1.2]
  Motor = DC Motor
  U2 = Voltage Regulator - 5V [package="TO220 [THT]"]
  US-Front = 28015 Ultrasonic Digital Sensor [package=THT]
  US-Seite = 28015 Ultrasonic Digital Sensor [package=THT]
  RPi-Akku = 4 x AAA Battery Mount
  Driver = Arduino Uno (Rev3) - ICSP
  Motor-Akku = 4 x AAA Battery Mount
  Bauteil2 = Pololu SImple High-Power Motor Controller 18v15 [part_number=MD03A]
  Lenkung = Basic Servo

nets:
  GND: Cortex.GND, US-Front.GND, US-Seite.GND, RPi-Akku.-, Bauteil2.GND3, Lenkung.gnd
  N1: Cortex.GIPO18, Lenkung.pulse
  N2: Cortex.GIPO15, Driver.D1/TX
  N3: Cortex.GIPO14, Driver.D0/RX
  5V: Cortex.5V, US-Front.5V, US-Seite.5V, RPi-Akku.+, Driver.5V
  N4: Motor.pin_1, Bauteil2.OUTA
  N5: Motor.pin_2, Bauteil2.OUTB
  N6: U2.input_voltage, Bauteil2.VIN1
  GND_2: U2.GND, Bauteil2.GND1
  N7: U2.output_voltage, Lenkung.vcc
  N8: US-Front.SIG, Driver.D7
  N9: US-Seite.SIG, Driver.D8
  N10: Driver.D11_PWM/MOSI, Bauteil2.RC1
  GND_3: Driver.GND, Bauteil2.GND2
  N11: Motor-Akku.-, Bauteil2.GND4
  N12: Motor-Akku.+, Bauteil2.VIN2

custom parts:
  28015 Ultrasonic Digital Sensor: This is the 28015 ultrasonic digital sensor from parallax inf
  Pololu SImple High-Power Motor Controller 18v15: The Pololu simple high-power motor driver Controller integrated circuits from ST. http://www.pololu.com/catalog/product/1376
