# Fritzing sketch Aufbau (saved by Fritzing 0.9.3b)

parts:
  Bauteil1 = Arduino Uno (Rev3) - ICSP
  Raspberry_Pi_1 = Raspberry Pi 3 [part_number=RPI-3-V1.2]
  J1 = Basic Servo
  U1 = 28015 Ultrasonic Digital Sensor [package=THT]

nets:
  GND: Bauteil1.GND, U1.GND
  N1: Bauteil1.D7, U1.SIG
  5V: Bauteil1.5V, U1.5V
  GND_2: Raspberry_Pi_1.GND, Raspberry_Pi_1.GIPO18, Raspberry_Pi_1.GIPO14, J1.gnd, J1.pulse
  5V_2: Raspberry_Pi_1.5V, J1.vcc

custom parts:
  28015 Ultrasonic Digital Sensor: This is the 28015 ultrasonic digital sensor from parallax inf
